# Fritzing sketch Morse (saved by Fritzing 0.9.3b)
breadboards: 1

parts:
  LED1 = smd LED [color="Yellow (595nm)" package="1206 [SMD]"]
  LED2 = smd LED [color="Blue (525nm)" package="1206 [SMD]"]
  R1 = Resistor [tolerance=±5% resistance=330 package="0402 [SMD]"]
  R2 = Resistor [tolerance=±5% resistance=330 package="0402 [SMD]"]
  Raspberry_Pi_3B+ = Raspberry Pi 3 [part_number=RPI-3-V1.2]

nets:
  N1: LED1.cathode, R2.Pin_1
  N2: LED1.anode, Raspberry_Pi_3B+.GPIO18
  N3: LED2.cathode, R1.Pin_1
  N4: LED2.anode, Raspberry_Pi_3B+.GPIO17
  N5: R1.Pin_0, R2.Pin_0, Raspberry_Pi_3B+.GND
